// Logisim project 3.circ as structural Verilog: 1 circuit, main circuit main
module main (
  input  d,
  input  c,
  input  b,
  input  a,
  output out_5
);

  wire not_1_out, not_2_out;

  not not_1 (not_1_out, 1'b1);
  not not_2 (not_2_out, d);
  Multiplexer #(.select(3), .enable("false")) multiplexer_1 (
    .in0(not_2_out), .in1(d), .in2(not_1_out), .in3(not_1_out), .in4(not_2_out), .in5(not_1_out),
    .in6(not_1_out), .in7(1'b1), .out(out_5), .sel({a, b, c}));
endmodule
