// Logisim project 5.circ as structural Verilog: 1 circuit, main circuit main
module main (
  input  x1,
  input  input_Carry,
  input  x0,
  output Sum,
  output Carry
);

  wire not_1_out, not_2_out;

  not not_1 (not_1_out, 1'b1);
  not not_2 (not_2_out, input_Carry);
  Multiplexer #(.select(2), .disabled(0), .enable("false")) multiplexer_1 (
    .in0(input_Carry), .in1(not_2_out), .in2(not_2_out), .in3(input_Carry), .out(Sum), .sel({x1, x0}));
  Multiplexer #(.select(2), .disabled(0), .enable("false")) multiplexer_2 (
    .in0(not_1_out), .in1(input_Carry), .in2(input_Carry), .in3(1'b1), .out(Carry), .sel({x1, x0}));
endmodule
