// Logisim project 6.circ as structural Verilog: 6 circuits, main circuit main
module main (
  input  UP,
  input  RESET
);

  wire _0_d0p, _1_d1m, _1_d1p, _2_d2m, _2_d2p, _3_d3m, _3_d3p, and_1_out, and_2_out, and_3_out, and_4_out,
       and_5_out, and_6_out, and_7_out, and_8_out, and_9_out, and_10_out, clock_1_out, D0_q, D1_q, D2_q,
       D3_q, decoder_1_out0, decoder_1_out1, decoder_1_out2, decoder_1_out3, nor_1_out, or_1_out, or_2_out,
       or_3_out;

  Clock clock_1 (.out(clock_1_out));
  Decoder #(.select(2), .disabled(0), .enable("false")) decoder_1 (
    .out0(decoder_1_out0), .out1(decoder_1_out1), .out2(decoder_1_out2), .out3(decoder_1_out3),
    .sel({UP, RESET}));
  nor nor_1 (nor_1_out, decoder_1_out1, decoder_1_out3);
  _3 _3 (.D3(D3_q), .D2(D2_q), .D1(D1_q), .D0(D0_q), .D3P(_3_d3p), .D3M(_3_d3m));
  and and_1 (and_1_out, _3_d3m, decoder_1_out0);
  and and_2 (and_2_out, decoder_1_out2, _3_d3p);
  or or_1 (or_1_out, and_1_out, and_2_out);
  and and_3 (and_3_out, or_1_out, nor_1_out);
  D_Flip_Flop D3 (.clk(clock_1_out), .D(and_3_out), .Q(D3_q));  // open: Qn, preset, en, reset
  _2 _2 (.D2(D2_q), .D1(D1_q), .D0(D0_q), .D2M(_2_d2m), .D2P(_2_d2p));
  and and_4 (and_4_out, _2_d2m, decoder_1_out0);
  and and_5 (and_5_out, decoder_1_out2, _2_d2p);
  or or_2 (or_2_out, and_5_out, and_4_out);
  and and_6 (and_6_out, or_2_out, nor_1_out);
  D_Flip_Flop D2 (.clk(clock_1_out), .D(and_6_out), .Q(D2_q));  // open: Qn, preset, en, reset
  _1 _1 (.D0(D0_q), .D1(D1_q), .D1P(_1_d1p), .D1M(_1_d1m));
  and and_7 (and_7_out, _1_d1m, decoder_1_out0);
  and and_8 (and_8_out, decoder_1_out2, _1_d1p);
  or or_3 (or_3_out, and_8_out, and_7_out);
  and and_9 (and_9_out, or_3_out, nor_1_out);
  D_Flip_Flop D1 (.clk(clock_1_out), .D(and_9_out), .Q(D1_q));  // open: Qn, preset, en, reset
  _0 _0 (.D0(D0_q), .D0P(_0_d0p));
  and and_10 (and_10_out, nor_1_out, _0_d0p);
  D_Flip_Flop D0 (.clk(clock_1_out), .D(and_10_out), .Q(D0_q));  // open: Qn, preset, en, reset
endmodule

module _0 (
  input  D0,
  output D0P
);

  not not_1 (D0P, D0);
endmodule

module _00 (
  input  D0,
  output D0P
);

  not not_1 (D0P, D0);
endmodule

module _1 (
  input  D0,
  input  D1,
  output D1P,
  output D1M
);

  xor xor_1 (D1P, D1, D0);
  xnor xnor_1 (D1M, D1, D0);
endmodule

module _2 (
  input  D2,
  input  D1,
  input  D0,
  output D2M,
  output D2P
);

  wire and_1_out, and_2_out, and_3_out, and_4_out, and_5_out, and_6_out, not_1_out, not_2_out, not_3_out,
       not_4_out, not_5_out, not_6_out;

  not not_1 (not_1_out, D2);
  not not_2 (not_2_out, D1);
  not not_3 (not_3_out, D0);
  not not_4 (not_4_out, D2);
  not not_5 (not_5_out, D1);
  not not_6 (not_6_out, D0);
  and and_1 (and_1_out, not_1_out, not_2_out, not_3_out);
  and and_2 (and_2_out, D2, D0);
  and and_3 (and_3_out, D2, D1);
  and and_4 (and_4_out, not_4_out, D1, D0);
  and and_5 (and_5_out, D2, not_5_out);
  and and_6 (and_6_out, D2, not_6_out);
  or or_1 (D2M, and_1_out, and_2_out, and_3_out);
  or or_2 (D2P, and_4_out, and_5_out, and_6_out);
endmodule

module _3 (
  input  D3,
  input  D2,
  input  D1,
  input  D0,
  output D3P,
  output D3M
);

  wire and_1_out, and_2_out, and_3_out, and_4_out, and_5_out, and_6_out, and_7_out, and_8_out, not_1_out,
       not_2_out, not_3_out, not_4_out, not_5_out, not_6_out, not_7_out, not_8_out;

  not not_1 (not_1_out, D3);
  not not_2 (not_2_out, D2);
  not not_3 (not_3_out, D1);
  not not_4 (not_4_out, D0);
  not not_5 (not_5_out, D3);
  not not_6 (not_6_out, D2);
  not not_7 (not_7_out, D1);
  not not_8 (not_8_out, D0);
  and and_1 (and_1_out, not_1_out, D2, D1, D0);
  and and_2 (and_2_out, D3, not_2_out);
  and and_3 (and_3_out, D3, not_3_out);
  and and_4 (and_4_out, D3, not_4_out);
  and and_5 (and_5_out, not_5_out, not_6_out, not_7_out, not_8_out);
  and and_6 (and_6_out, D3, D0);
  and and_7 (and_7_out, D3, D1);
  and and_8 (and_8_out, D3, D2);
  or or_1 (D3P, and_1_out, and_2_out, and_3_out, and_4_out);
  or or_2 (D3M, and_5_out, and_6_out, and_7_out, and_8_out);
endmodule
